// Digital circuit hardware.dig as structural Verilog
module hardware (
  input  clk,
  input  [15:0] in_2,
  input  in_3,
  input  [3:0] in_4,
  input  [3:0] in_5,
  input  [3:0] in_6
);

  wire [15:0] registerfile_1_da, registerfile_1_db;

  RegisterFile #(.AddrBits(4), .Bits(16)) registerfile_1 (
    .Din(in_2), .we(in_3), .Rw(in_4), .C(clk), .Ra(in_5), .Rb(in_6), .Da(registerfile_1_da),
    .Db(registerfile_1_db));
  // Probe on registerfile_1_da
  // Probe on registerfile_1_db
endmodule
